# Fritzing sketch esp32-lightsensor (saved by Fritzing 0.9.10b)
perfboards: 1

parts:
  U1 = ESP32-38PinWide [part_number=ESP32-38PinWide]
  U2 = BH1750
  M1 = BMP280

nets:
  VCC: U1.3.3, U2.VCC, M1.VIN
  GND: U1.GND, U2.GND, M1.GND
  N1: U1.GPIO21, U2.SDA, M1.SDA
  N2: U1.GPIO22, U2.SCL, M1.SCL

custom parts:
  ESP32-38PinWide: Generic 38-Pin ESP32 with wide format (only access to one side of pins on a breadboard) based on Stephen Lilley's HiLetgo ESP-WROOM-32 ESP32 ESP-32S Development Board.
  BH1750: Light Sensor
  BMP280: Temperature Humidity Barometric presure Sensor, I2C
